// Digital circuit Controlador_Display1.dig as structural Verilog
module Controlador_Display1 (
  input  A,
  input  B,
  input  C,
  output a_2,
  output b_2,
  output c_2,
  output d,
  output e,
  output f,
  output g
);

  wire and_1_out, and_2_out, and_3_out, and_4_out, and_5_out, and_6_out, and_7_out, not_1_out, not_2_out,
       not_3_out;

  not not_1 (not_1_out, B);
  not not_2 (not_2_out, C);
  not not_3 (not_3_out, A);
  and and_1 (and_1_out, A, not_1_out);
  and and_2 (and_2_out, A, not_2_out);
  and and_3 (and_3_out, not_1_out, not_2_out);
  or or_1 (c_2, not_1_out, not_2_out);
  and and_4 (and_4_out, C, not_1_out, not_3_out);
  and and_5 (and_5_out, B, not_3_out, not_2_out);
  and and_6 (and_6_out, not_1_out, not_3_out);
  and and_7 (and_7_out, not_3_out, not_2_out);
  or or_2 (a_2, and_1_out, and_2_out);
  or or_3 (b_2, a_2, and_3_out);
  or or_4 (d, and_4_out, and_5_out);
  or or_5 (f, and_6_out, and_7_out);

  assign e = d;
  assign g = f;

  // Other names for the same wires on the sheet: a_t = a_2
endmodule
