// Digital circuit Controlador_Display2.dig as structural Verilog
module Controlador_Display2 (
  input  A,
  input  B,
  input  C,
  output a_2,
  output b_2,
  output c_2,
  output d,
  output e,
  output f,
  output g
);

  wire and_1_out, and_2_out, and_3_out, and_4_out, and_5_out, and_6_out, and_7_out, and_8_out, not_2_out,
       not_3_out;

  not not_1 (f, B);
  not not_2 (not_2_out, C);
  not not_3 (not_3_out, A);
  and and_1 (and_1_out, A, not_2_out);
  and and_2 (and_2_out, not_2_out, B);
  and and_3 (and_3_out, not_3_out, not_2_out);
  and and_4 (and_4_out, C, A, f);
  and and_5 (and_5_out, not_2_out, A);
  and and_6 (and_6_out, C, f, not_3_out);
  and and_7 (and_7_out, not_2_out, B, A);
  and and_8 (and_8_out, not_2_out, f, not_3_out);
  or or_1 (a_2, f, and_1_out);
  or or_2 (b_2, and_2_out, and_3_out, and_4_out);
  or or_3 (c_2, and_3_out, f);
  or or_4 (d, and_5_out, and_6_out);
  or or_5 (e, and_7_out, and_4_out, and_8_out);

  assign g = a_2;
endmodule
