// Digital circuit Laboratorio_1.dig as structural Verilog
module Laboratorio_1 (
);

  wire A, B, C, Controlador_Display_1_a_2, Controlador_Display_1_b_2, Controlador_Display_1_c_2,
       Controlador_Display_1_d, Controlador_Display_1_e, Controlador_Display_1_f, Controlador_Display_1_g,
       Controlador_Display_2_a_2, Controlador_Display_2_b_2, Controlador_Display_2_c_2,
       Controlador_Display_2_d, Controlador_Display_2_e, Controlador_Display_2_f, Controlador_Display_2_g,
       notconnected_1_out, notconnected_2_out;

  DipSwitch dipswitch_1 (.out(C));
  DipSwitch dipswitch_2 (.out(B));
  DipSwitch dipswitch_3 (.out(A));
  Controlador_Display2 Controlador_Display_2 (
    .A(A), .B(B), .C(C), .a_2(Controlador_Display_2_a_2), .b_2(Controlador_Display_2_b_2),
    .c_2(Controlador_Display_2_c_2), .d(Controlador_Display_2_d), .e(Controlador_Display_2_e),
    .f(Controlador_Display_2_f), .g(Controlador_Display_2_g));
  Controlador_Display1 Controlador_Display_1 (
    .A(A), .B(B), .C(C), .a_2(Controlador_Display_1_a_2), .b_2(Controlador_Display_1_b_2),
    .c_2(Controlador_Display_1_c_2), .d(Controlador_Display_1_d), .e(Controlador_Display_1_e),
    .f(Controlador_Display_1_f), .g(Controlador_Display_1_g));
  Seven_Seg seven_seg_1 (
    .a(Controlador_Display_1_a_2), .b(Controlador_Display_1_b_2), .c(Controlador_Display_1_c_2),
    .d(Controlador_Display_1_d), .e(Controlador_Display_1_e), .f(Controlador_Display_1_f),
    .g(Controlador_Display_1_g), .dp(notconnected_1_out));
  // NotConnected on notconnected_1_out
  Seven_Seg seven_seg_2 (
    .a(Controlador_Display_2_a_2), .b(Controlador_Display_2_b_2), .c(Controlador_Display_2_c_2),
    .d(Controlador_Display_2_d), .e(Controlador_Display_2_e), .f(Controlador_Display_2_f),
    .g(Controlador_Display_2_g), .dp(notconnected_2_out));
  // NotConnected on notconnected_2_out
endmodule
